// Logisim project ALU.circ as structural Verilog: 1 circuit, main circuit main
module main (
  input  in_1,
  input  in_2,
  input  in_3,
  input  in_4,
  input  [1:0] in_5,
  input  in_6,
  input  [1:0] in_7,
  input  in_8,
  input  [1:0] in_9,
  input  in_10,
  input  in_11,
  input  in_12,
  input  in_13,
  input  [1:0] in_14,
  input  in_15
);

  wire and_1_out, and_2_out, and_3_out, and_4_out, clock_1_out, demultiplexer_1_out0, demultiplexer_1_out1,
       demultiplexer_1_out2, demultiplexer_1_out3, multiplexer_5_out, multiplexer_6_out, multiplexer_7_out,
       multiplexer_8_out, multiplexer_9_out, multiplexer_10_out, multiplexer_11_out, multiplexer_12_out,
       or_1_out, or_2_out, or_3_out, or_4_out, register_1_q, register_2_q, register_3_q, register_4_q,
       register_5_q, register_6_q, register_7_q, register_8_q, register_9_q, register_10_q, register_11_q,
       register_12_q, register_13_q, register_14_q, register_15_q, register_16_q, xor_1_out, xor_2_out,
       xor_3_out, xor_4_out;

  Register #(.width(1)) register_1 (.D(in_1), .Q(register_1_q), .clk(demultiplexer_1_out0));  // open: en, clr
  Register #(.width(1)) register_2 (.D(in_2), .Q(register_2_q), .clk(demultiplexer_1_out0));  // open: en, clr
  Register #(.width(1)) register_3 (.D(in_3), .Q(register_3_q), .clk(demultiplexer_1_out0));  // open: en, clr
  Register #(.width(1)) register_4 (.D(in_4), .Q(register_4_q), .clk(demultiplexer_1_out0));  // open: en, clr
  Multiplexer #(.select(2)) multiplexer_1 (
    .in0(register_1_q), .in1(register_5_q), .in2(register_9_q), .in3(register_13_q), .out(in_1), .sel(in_9),
    .en(in_10));
  LED led_1 (.in(in_1));
  Register #(.width(1)) register_5 (.D(in_1), .Q(register_5_q), .clk(demultiplexer_1_out1));  // open: en, clr
  Register #(.width(1)) register_6 (.D(in_2), .Q(register_6_q), .clk(demultiplexer_1_out1));  // open: en, clr
  Register #(.width(1)) register_7 (.D(in_3), .Q(register_7_q), .clk(demultiplexer_1_out1));  // open: en, clr
  Register #(.width(1)) register_8 (.D(in_4), .Q(register_8_q), .clk(demultiplexer_1_out1));  // open: en, clr
  Register #(.width(1)) register_9 (.D(in_1), .Q(register_9_q), .clk(demultiplexer_1_out2));  // open: en, clr
  Register #(.width(1)) register_10 (.D(in_2), .Q(register_10_q), .clk(demultiplexer_1_out2));  // open: en, clr
  Register #(.width(1)) register_11 (.D(in_3), .Q(register_11_q), .clk(demultiplexer_1_out2));  // open: en, clr
  Register #(.width(1)) register_12 (.D(in_4), .Q(register_12_q), .clk(demultiplexer_1_out2));  // open: en, clr
  Multiplexer #(.select(2)) multiplexer_2 (
    .in0(register_2_q), .in1(register_6_q), .in2(register_10_q), .in3(register_14_q), .out(in_2), .sel(in_9),
    .en(in_10));
  LED led_2 (.in(in_2));
  Register #(.width(1)) register_13 (.D(in_1), .Q(register_13_q), .clk(demultiplexer_1_out3));  // open: en, clr
  Register #(.width(1)) register_14 (.D(in_2), .Q(register_14_q), .clk(demultiplexer_1_out3));  // open: en, clr
  Register #(.width(1)) register_15 (.D(in_3), .Q(register_15_q), .clk(demultiplexer_1_out3));  // open: en, clr
  Register #(.width(1)) register_16 (.D(in_4), .Q(register_16_q), .clk(demultiplexer_1_out3));  // open: en, clr
  Multiplexer #(.select(2)) multiplexer_3 (
    .in0(register_3_q), .in1(register_7_q), .in2(register_11_q), .in3(register_15_q), .out(in_3), .sel(in_9),
    .en(in_10));
  LED led_3 (.in(in_3));
  Multiplexer #(.select(2)) multiplexer_4 (
    .in0(register_4_q), .in1(register_8_q), .in2(register_12_q), .in3(register_16_q), .out(in_4), .sel(in_9),
    .en(in_10));
  LED led_4 (.in(in_4));
  Demultiplexer #(.select(2)) demultiplexer_1 (
    .out0(demultiplexer_1_out0), .out1(demultiplexer_1_out1), .out2(demultiplexer_1_out2),
    .out3(demultiplexer_1_out3), .in(clock_1_out), .sel(in_5), .en(in_6));
  Clock clock_1 (.out(clock_1_out));
  Multiplexer #(.select(2)) multiplexer_5 (
    .in0(register_1_q), .in1(register_5_q), .in2(register_9_q), .in3(register_13_q), .out(multiplexer_5_out),
    .sel(in_7), .en(in_15));
  LED led_5 (.in(multiplexer_5_out));
  Multiplexer #(.select(2)) multiplexer_6 (
    .in0(register_2_q), .in1(register_6_q), .in2(register_10_q), .in3(register_14_q),
    .out(multiplexer_6_out), .sel(in_7), .en(in_15));
  Multiplexer #(.select(2)) multiplexer_7 (
    .in0(register_3_q), .in1(register_7_q), .in2(register_11_q), .in3(register_15_q),
    .out(multiplexer_7_out), .sel(in_7), .en(in_15));
  LED led_6 (.in(multiplexer_8_out));
  Multiplexer #(.select(2)) multiplexer_8 (
    .in0(register_4_q), .in1(register_8_q), .in2(register_12_q), .in3(register_16_q),
    .out(multiplexer_8_out), .sel(in_7), .en(in_15));
  Multiplexer #(.select(2)) multiplexer_9 (
    .in0(register_1_q), .in1(register_5_q), .in2(register_9_q), .in3(register_13_q), .out(multiplexer_9_out),
    .sel(in_14), .en(in_15));
  LED led_7 (.in(multiplexer_9_out));
  Multiplexer #(.select(2)) multiplexer_10 (
    .in0(register_2_q), .in1(register_6_q), .in2(register_10_q), .in3(register_14_q),
    .out(multiplexer_10_out), .sel(in_14), .en(in_15));
  LED led_8 (.in(multiplexer_10_out));
  Multiplexer #(.select(2)) multiplexer_11 (
    .in0(register_3_q), .in1(register_7_q), .in2(register_11_q), .in3(register_15_q),
    .out(multiplexer_11_out), .sel(in_14), .en(in_15));
  LED led_9 (.in(multiplexer_11_out));
  LED led_10 (.in(multiplexer_12_out));
  Multiplexer #(.select(2)) multiplexer_12 (
    .in0(register_4_q), .in1(register_8_q), .in2(register_12_q), .in3(register_16_q),
    .out(multiplexer_12_out), .sel(in_14), .en(in_15));
  LED led_11 (.in(multiplexer_6_out));
  LED led_12 (.in(multiplexer_7_out));
  assign in_1 = in_8 ? and_1_out : 1'bz;  // Controlled_Buffer controlled_buffer_1
  and and_1 (and_1_out, multiplexer_5_out, multiplexer_9_out);
  assign in_2 = in_8 ? and_2_out : 1'bz;  // Controlled_Buffer controlled_buffer_2
  and and_2 (and_2_out, multiplexer_6_out, multiplexer_10_out);
  and and_3 (and_3_out, multiplexer_7_out, multiplexer_11_out);
  assign in_3 = in_8 ? and_3_out : 1'bz;  // Controlled_Buffer controlled_buffer_3
  assign in_4 = in_8 ? and_4_out : 1'bz;  // Controlled_Buffer controlled_buffer_4
  and and_4 (and_4_out, multiplexer_8_out, multiplexer_12_out);
  assign in_1 = in_11 ? or_1_out : 1'bz;  // Controlled_Buffer controlled_buffer_5
  or or_1 (or_1_out, multiplexer_5_out, multiplexer_9_out);
  or or_2 (or_2_out, multiplexer_6_out, multiplexer_10_out);
  assign in_2 = in_11 ? or_2_out : 1'bz;  // Controlled_Buffer controlled_buffer_6
  assign in_3 = in_11 ? or_3_out : 1'bz;  // Controlled_Buffer controlled_buffer_7
  or or_3 (or_3_out, multiplexer_7_out, multiplexer_11_out);
  or or_4 (or_4_out, multiplexer_8_out, multiplexer_12_out);
  assign in_4 = in_11 ? or_4_out : 1'bz;  // Controlled_Buffer controlled_buffer_8
  xor xor_1 (xor_1_out, multiplexer_5_out, multiplexer_9_out);
  assign in_1 = in_12 ? xor_1_out : 1'bz;  // Controlled_Buffer controlled_buffer_9
  assign in_2 = in_12 ? xor_2_out : 1'bz;  // Controlled_Buffer controlled_buffer_10
  xor xor_2 (xor_2_out, multiplexer_6_out, multiplexer_10_out);
  xor xor_3 (xor_3_out, multiplexer_7_out, multiplexer_11_out);
  assign in_3 = in_12 ? xor_3_out : 1'bz;  // Controlled_Buffer controlled_buffer_11
  xor xor_4 (xor_4_out, multiplexer_8_out, multiplexer_12_out);
  assign in_1 = in_13 ? ~multiplexer_5_out : 1'bz;  // Controlled_Inverter controlled_inverter_1
  assign in_2 = in_13 ? ~multiplexer_6_out : 1'bz;  // Controlled_Inverter controlled_inverter_2
  assign in_3 = in_13 ? ~multiplexer_7_out : 1'bz;  // Controlled_Inverter controlled_inverter_3
  LED led_13 (.in(in_4));
  assign in_4 = in_12 ? xor_4_out : 1'bz;  // Controlled_Buffer controlled_buffer_12
  assign in_4 = in_13 ? ~multiplexer_8_out : 1'bz;  // Controlled_Inverter controlled_inverter_4

  // Notes on the sheet:
  //   Registro 00
  //   Registro 01
  //   Registro 10
  //   Registro 11
  //   Indice de entrada
  //   Reloj
endmodule
